// Logisim project LAB-2.circ as structural Verilog: 4 circuits, main circuit main
module main (
  input  A,
  input  A_2,
  input  A_3,
  input  A_4,
  input  B,
  input  B_2,
  input  A_5,
  input  A_6,
  input  B_3,
  input  B_4,
  input  A_7,
  input  A_8,
  input  B_5,
  input  B_6,
  input  A_9,
  input  B_7,
  input  A_10,
  input  A_11,
  input  B_8,
  input  B_9,
  input  A_12,
  input  B_10,
  input  A_13,
  input  A_14,
  input  B_11,
  input  B_12,
  input  A_15,
  input  B_13,
  input  C,
  output A_prime,
  output A_prime_2,
  output AB,
  output AB_2,
  output A_B,
  output A_prime_B_prime__prime___A_B,
  output A_B__prime,
  output out_37,
  output out_38,
  output out_39,
  output AB__A_B__prime__prime,
  output out_41,
  output out_42,
  output out_43,
  output out_44
);

  wire ic7404_1_out_5, ic7408_1_out_8, ic7408_1_out_9, nand_2_out, nand_3_out, nand_4_out, nand_5_out,
       nand_6_out, nand_9_out, nand_10_out, nand_11_out, nand_12_out, nand_13_out, nand_14_out, nand_15_out,
       nand_18_out, nor_1_out, nor_2_out, nor_3_out, nor_4_out, nor_5_out, nor_6_out, nor_7_out;

  nand nand_1 (A_prime_2, A_2, A_2);
  nand nand_2 (nand_2_out, A_4, B_2);
  nand nand_3 (nand_3_out, A_5, A_5);
  nand nand_4 (nand_4_out, B_4, B_4);
  nand nand_5 (nand_5_out, A_7, A_7);
  nand nand_6 (nand_6_out, B_6, B_6);
  IC7404 ic7404_1 (.in_2(C), .out_5(ic7404_1_out_5));  // open: in_1, out_4, in_3, out_6
  nand nand_7 (AB_2, nand_2_out, nand_2_out);
  nand nand_8 (A_prime_B_prime__prime___A_B, nand_3_out, nand_4_out);
  nand nand_9 (nand_9_out, nand_5_out, nand_6_out);
  nand nand_10 (nand_10_out, A_9, B_7);
  nor nor_1 (nor_1_out, A_11, A_11);
  nor nor_2 (nor_2_out, B_9, B_9);
  nor nor_3 (nor_3_out, A_11, B_9);
  nand nand_11 (nand_11_out, A_12, B_10);
  nor nor_4 (nor_4_out, A_14, B_12);
  nor nor_5 (nor_5_out, A_14, nor_4_out);
  nor nor_6 (nor_6_out, nor_4_out, B_12);
  IC7408 ic7408_1 (
    .in_3(A_15), .out_8(ic7408_1_out_8), .in_4(C), .in_5(B_13), .out_9(ic7408_1_out_9), .in_6(ic7404_1_out_5));  // open: in_1, out_7, in_2
  nand nand_12 (nand_12_out, A_9, nand_10_out);
  nand nand_13 (nand_13_out, nand_10_out, B_7);
  nor nor_7 (nor_7_out, nor_1_out, nor_2_out);
  nand nand_14 (nand_14_out, A_12, nand_11_out);
  nand nand_15 (nand_15_out, nand_11_out, B_10);
  nand nand_16 (out_37, nand_9_out, nand_9_out);
  nor nor_8 (AB__A_B__prime__prime, nor_7_out, nor_3_out);
  nor nor_9 (out_43, nor_5_out, nor_6_out);
  IC7432 ic7432_1 (
    .in_1(ic7408_1_out_8), .in_2(ic7408_1_out_9), .out_7(out_44));  // open: in_3, out_8, in_4, in_5, out_9, in_6
  nand nand_17 (out_38, nand_12_out, nand_13_out);
  nand nand_18 (nand_18_out, nand_14_out, nand_15_out);
  not not_1 (A_prime, A);
  and and_1 (AB, A_3, B);
  or or_1 (A_B, A_6, B_3);
  nor nor_10 (A_B__prime, A_8, B_5);
  nand nand_19 (out_41, nand_18_out, nand_18_out);
  xor xor_1 (out_39, A_10, B_8);
  xnor xnor_1 (out_42, A_13, B_11);

  // Notes on the sheet:
  //   1.
  //   2.
  //   3.
  //   4.
  //   XNOR Using NAND
  //   XOR Using NOR
  //   XNOR Using NAND
  //   XNOR Using NOR
  //   (A.A)'
  //   (AB)'
  //   A'
  //   B'
  //   A'
  //   B'
  //   Figure D2 : A Combinational Circuit With IC Diagram
  //   IC7404
  //   (AB)'
  //   A'
  //   B'
  //   (A+B)'
  //   (AB)'
  //   (A+B)'
  //   C'
  //   (A'B')' = A+B
  //   IC7408
  //   B.C'
  //   (A.(AB)')' = A'+AB
  //   (B.(AB)')' = B'+AB
  //   A.B
  //   (A.(AB)')'
  //   (B.(AB)')'
  //   (A+(A+B)')'
  //   (B+(A+B)')'
  //   AC
  //   ((A+B).(A+B))'=(A+B)'
  //   AC+BC'
  //   IC7432
  //   ((A+(A+B)')'+(B+(A+B)')')'
  //   Proof:
  //   ((A'+AB).(B'+AB))'
  //   ((A.(AB)')'.(B.(AB)')')'
  //   Proof:
  //   Proof:
endmodule

module IC7408 (
  input  in_1,
  input  in_2,
  input  in_3,
  input  in_4,
  input  in_5,
  input  in_6,
  output out_7,
  output out_8,
  output out_9
);

  wire nand_1_out, nand_2_out, nand_3_out;

  nand nand_1 (nand_1_out, in_1, in_2);
  nand nand_2 (nand_2_out, in_3, in_4);
  nand nand_3 (nand_3_out, in_5, in_6);
  nor nor_1 (out_7, nand_1_out, nand_1_out);
  nor nor_2 (out_8, nand_2_out, nand_2_out);
  nor nor_3 (out_9, nand_3_out, nand_3_out);
endmodule

module IC7432 (
  input  in_1,
  input  in_2,
  input  in_3,
  input  in_4,
  input  in_5,
  input  in_6,
  output out_7,
  output out_8,
  output out_9
);

  wire nor_1_out, nor_2_out, nor_3_out, nor_4_out, nor_5_out, nor_6_out;

  nor nor_1 (nor_1_out, in_1, in_1);
  nor nor_2 (nor_2_out, in_2, in_2);
  nor nor_3 (nor_3_out, in_3, in_3);
  nor nor_4 (nor_4_out, in_4, in_4);
  nor nor_5 (nor_5_out, in_5, in_5);
  nor nor_6 (nor_6_out, in_6, in_6);
  nand nand_1 (out_7, nor_1_out, nor_2_out);
  nand nand_2 (out_8, nor_3_out, nor_4_out);
  nand nand_3 (out_9, nor_5_out, nor_6_out);
endmodule

module IC7404 (
  input  in_1,
  input  in_2,
  input  in_3,
  output out_4,
  output out_5,
  output out_6
);

  nand nand_1 (out_4, in_1, in_1);
  nand nand_2 (out_5, in_2, in_2);
  nor nor_1 (out_6, in_3, in_3);
endmodule
